# Fritzing sketch principe marelle (saved by Fritzing 0.9.3b)

parts:
  Teensy1 = Teensy 2.0
  Composant1 = Logic Level Converter
  Composant2 = Logic Level Converter
  Composant3 = Logic Level Converter
  Composant4 = Logic Level Converter
  XLR1 = XLR3_NCFAH2 [package=xlr3_nc3fah2]
  XLR2 = XLR3_NCFAH2 [package=xlr3_nc3fah2]
  Teensy2 = Teensy 2.0
  Composant5 = Logic Level Converter
  Composant6 = Logic Level Converter
  Composant7 = Logic Level Converter
  Composant8 = Logic Level Converter
  XLR3 = XLR3_NCFAH2 [package=xlr3_nc3fah2]
  XLR4 = XLR3_NCFAH2 [package=xlr3_nc3fah2]
  Teensy3 = Teensy 2.0
  Composant9 = Logic Level Converter
  Composant10 = Logic Level Converter
  Composant11 = Logic Level Converter
  Composant12 = Logic Level Converter
  XLR5 = XLR3_NCFAH2 [package=xlr3_nc3fah2]
  XLR6 = XLR3_NCFAH2 [package=xlr3_nc3fah2]
  U1 = Mini-USB _B_ connector with 5th pin broken out. [package=usb-micro_b]  # not connected

nets:
  GND: Teensy1.GND, Composant1.GND, Composant2.GND, Composant3.GND, Composant4.GND, XLR1.3, XLR2.G
  N1: Teensy1.B3, Composant4.RX_LV
  N2: Teensy1.B7, Composant4.TX_LV
  N3: Teensy1.D0, Composant3.RX_LV
  N4: Teensy1.D1, Composant3.TX_LV
  N5: Teensy1.D2, Composant2.RX_LV
  N6: Teensy1.D3, Composant2.TX_LV
  N7: Teensy1.C6, Composant1.RX_LV
  N8: Teensy1.C7, Composant1.TX_LV
  N9: Teensy1.B4, XLR1.2
  N10: Teensy1.B5, XLR2.1
  N11: Teensy1.VCC, Composant1.RX2_LV, Composant2.RX2_LV, Composant3.RX2_LV, Composant4.RX2_LV, XLR1.G
  GND_2: Teensy2.GND, Composant5.GND, Composant6.GND, Composant7.GND, Composant8.GND, XLR3.3, XLR4.G
  N12: Teensy2.B3, Composant6.RX_LV
  N13: Teensy2.B7, Composant6.TX_LV
  N14: Teensy2.D0, Composant8.RX_LV
  N15: Teensy2.D1, Composant8.TX_LV
  N16: Teensy2.D2, Composant7.RX_LV
  N17: Teensy2.D3, Composant7.TX_LV
  N18: Teensy2.C6, Composant5.RX_LV
  N19: Teensy2.C7, Composant5.TX_LV
  N20: Teensy2.B4, XLR3.2
  N21: Teensy2.B5, XLR4.1
  N22: Teensy2.VCC, Composant5.RX2_LV, Composant6.RX2_LV, Composant7.RX2_LV, Composant8.RX2_LV, XLR3.G, XLR4.3
  GND_3: Teensy3.GND, Composant9.GND, Composant10.GND, Composant11.GND, Composant12.GND, XLR5.3, XLR6.G
  N23: Teensy3.B3, Composant10.RX_LV
  N24: Teensy3.B7, Composant10.TX_LV
  N25: Teensy3.D0, Composant12.RX_LV
  N26: Teensy3.D1, Composant12.TX_LV
  N27: Teensy3.D2, Composant11.RX_LV
  N28: Teensy3.D3, Composant11.TX_LV
  N29: Teensy3.C6, Composant9.RX_LV
  N30: Teensy3.C7, Composant9.TX_LV
  N31: Teensy3.B4, XLR5.2
  N32: Teensy3.B5, XLR6.1
  N33: Teensy3.VCC, Composant9.RX2_LV, Composant10.RX2_LV, Composant11.RX2_LV, Composant12.RX2_LV, XLR5.G, XLR6.3

notes:
  RX
  (non utilisé)
  TX
  loadCell
  RX
  TX
  (non utilisé)
  ................................
  ................................
  ................................
  ....
  ....
  ....
  USB Midi
  (terminale)
